# Fritzing sketch diagram (saved by Fritzing 1.0.3b)

parts:
  U2 = ESP 32 DEVKIT DOIT
  RY1 = KF-301 Relay [package=THT]
  RY2 = KF-301 Relay [package=THT]
  RY3 = KF-301 Relay [package=THT]
  DHT2 = DHT11 Humitidy and Temperature Sensor (3 pins)
  LED1 = smd LED [color="Red (633nm)" package="1206 [SMD]"]
  LED2 = smd LED [color="Yellow (595nm)" package="1206 [SMD]"]
  Mod1 = generic-ac-power-supply [package=THT]
  TRM1 = Terminal 2pin
  TRM2 = Terminal 2pin
  TRM3 = Terminal 2pin
  TRM4 = Terminal 2pin
  S1 = Momentary Switch 6mm 2pin

nets:
  N1: U2.D18, U2.3V3, S1.1
  N2: U2.Vin, RY1.power, RY2.power, RY3.power, DHT2.Plus, Mod1.pin3#2
  GND: U2.GND, RY1.ground, RY2.ground, RY3.ground, DHT2.Gnd, LED2.cathode, Mod1.pin3#3, S1.2
  N3: U2.D13, U2.D14, RY1.signal, RY3.signal
  N4: U2.D12, RY2.signal
  N5: U2.D27, DHT2.Signal
  N6: U2.D26, LED1.anode
  N7: U2.D25, LED2.anode
  N8: RY1.C, RY2.C, RY3.C, Mod1.pin2, TRM1.pin_2
  N9: RY1.NO, TRM2.pin_1
  N10: RY2.NO, TRM3.pin_1
  N11: RY3.NO, TRM4.pin_1
  N12: Mod1.pin1, TRM1.pin_1, TRM2.pin_2, TRM3.pin_2, TRM4.pin_2

custom parts:
  KF-301 Relay: KF-301 SPDT Relay module using SRD-05VDC-SL-C relay.
  DHT11 Humitidy and Temperature Sensor (3 pins): DHT11 Humidity and Temperature Sensor (3 pins).
  generic-ac-power-supply: Generic ac power supply module. Use as is, or customize the svgs to fit your particular device (as they are all different.) Provides AC input and single DC output. PCB is generic and will need modifications if you intend to do a pcb mount.
  Terminal 2pin: 2-pin Terminal Block
  Momentary Switch 6mm 2pin: Momentary Switch 6mm 2 pin Button commonly used for reset or general input.
